// Logisim project lights_out_3.circ as structural Verilog: 1 circuit, main circuit main
module main (
);

  wire b0, b1, b2, b3, b4, b5, b6, b7, b8, l0, l1, l2, l3, l4, l5, l6, l7, l8, or_1_out, sigAnyPress,
       sigReset, sigWin;
  wire [2:0] sigAddr;
  wire [7:0] sigMoves;
  wire [8:0] multiplexer_1_out, sigMask, sigPreset, xor_1_out;

  Button button_1 (.out(sigReset));
  LED led_1 (.in(sigWin));
  Hex_Digit_Display #(.decimalPoint("false")) hex_digit_display_1 (.value(sigMoves[7:4]));
  Hex_Digit_Display #(.decimalPoint("false")) hex_digit_display_2 (.value(sigMoves[3:0]));
  assign xor_1_out = sigMask ^ {l8, l7, l6, l5, l4, l3, l2, l1, l0};  // XOR_Gate xor_1, 9 bits wide
  Multiplexer #(.width(9)) multiplexer_1 (.in0(xor_1_out), .in1(sigPreset), .out(multiplexer_1_out), .sel(sigReset));
  LED led_2 (.in(l0));
  LED led_3 (.in(l1));
  LED led_4 (.in(l4));
  LED led_5 (.in(l3));
  LED led_6 (.in(l6));
  LED led_7 (.in(l7));
  or or_1 (or_1_out, sigAnyPress, sigReset);
  LED led_8 (.in(l2));
  LED led_9 (.in(l5));
  LED led_10 (.in(l8));
  Register #(.trigger("falling"), .width(9)) register_1 (
    .D(multiplexer_1_out), .clk(or_1_out), .Q({l8, l7, l6, l5, l4, l3, l2, l1, l0}));  // open: en, clr
  nor nor_1 (sigWin, l0, l1, l2, l3, l4, l5, l6, l7, l8);
  Button button_2 (.out(b0));
  Button button_3 (.out(b1));
  Button button_4 (.out(b2));
  Button button_5 (.out(b3));
  Button button_6 (.out(b4));
  Button button_7 (.out(b5));
  Button button_8 (.out(b6));
  Button button_9 (.out(b7));
  Button button_10 (.out(b8));
  or or_2 (sigAnyPress, b0, b1, b2, b3, b4, b6, b5, b7, b8);
  Random #(.width(9)) random_1 (.next(1'b1), .clk(sigReset), .out(sigPreset));  // open: clr
  or or_3 (sigAddr[0], b1, b3, b5, b7);
  or or_4 (sigAddr[1], b2, b3, b6, b7);
  or or_5 (sigAddr[2], b4, b5, b6, b7);
  ROM #(.addrWidth(4), .dataWidth(9)) rom_1 (.addr({b8, sigAddr}), .data(sigMask));
  Counter counter_1 (.clr(sigReset), .clk(sigAnyPress), .Q(sigMoves));  // open: load, up, count, D, carry

  // Other names for the same wires on the sheet: sigAddr[3] = b8;
  //   sigState[8:0] = {l8, l7, l6, l5, l4, l3, l2, l1, l0}

  // Notes on the sheet:
  //   GAME CONTROLS
  //   Hit the button for New Random Board
  //   MOVE COUNTER
  //   VICTORY STATUS
  //   State Register
  //   Lights
  //   Select Poke Tool (Finger) -> Click any Light Button in the 3x3 Grid below!
  //   Win Detector
  //   LIGHTS OUT - 3x3 PUZZLE GAME
  //   Turn all lights off to WIN
  //   Buttons
  //   Button Encoder (9 to 4 bits)
  //   Random State Generator
  //   contents of rom_1 (hex, n*v repeats v):
  //   b 17 26 59 ba 134 c8 1d0 1a0
  //   BITMASK ROM (16x9)
  //   Moves Counter
endmodule
