// Logisim project lights_out_4x4.circ as structural Verilog: 1 circuit, main circuit main
module main (
);

  wire b0, b1, b2, b3, b4, b5, b6, b7, b8, b9, b10, b11, b12, b13, b14, b15, l0, l1, l2, l3, l4, l5, l6, l7,
       l8, l9, l10, l11, l12, l13, l14, l15, or_1_out, sigAnyPress, sigReset, sigWin;
  wire [3:0] sigAddr;
  wire [7:0] sigMoves;
  wire [15:0] multiplexer_1_out, sigMask, sigPreset, xor_1_out;

  Button button_1 (.out(sigReset));
  Hex_Digit_Display #(.decimalPoint("false")) hex_digit_display_1 (.value(sigMoves[7:4]));
  LED led_1 (.in(sigWin));
  Hex_Digit_Display #(.decimalPoint("false")) hex_digit_display_2 (.value(sigMoves[3:0]));
  assign xor_1_out = sigMask ^ {l15, l14, l13, l12, l11, l10, l9, l8, l7, l6, l5, l4, l3, l2, l1, l0};  // XOR_Gate xor_1, 16 bits wide
  or or_1 (or_1_out, sigAnyPress, sigReset);
  Multiplexer #(.width(16)) multiplexer_1 (.in0(xor_1_out), .in1(sigPreset), .out(multiplexer_1_out), .sel(sigReset));
  LED led_2 (.in(l4));
  LED led_3 (.in(l8));
  LED led_4 (.in(l0));
  LED led_5 (.in(l1));
  LED led_6 (.in(l2));
  LED led_7 (.in(l3));
  LED led_8 (.in(l5));
  LED led_9 (.in(l6));
  LED led_10 (.in(l7));
  LED led_11 (.in(l9));
  LED led_12 (.in(l10));
  LED led_13 (.in(l11));
  LED led_14 (.in(l12));
  LED led_15 (.in(l13));
  LED led_16 (.in(l14));
  LED led_17 (.in(l15));
  Register #(.trigger("falling"), .width(16)) register_1 (
    .D(multiplexer_1_out), .clk(or_1_out),
    .Q({l15, l14, l13, l12, l11, l10, l9, l8, l7, l6, l5, l4, l3, l2, l1, l0}));  // open: en, clr
  Button button_2 (.out(b0));
  Button button_3 (.out(b1));
  Button button_4 (.out(b5));
  Button button_5 (.out(b4));
  Button button_6 (.out(b8));
  Button button_7 (.out(b9));
  Button button_8 (.out(b12));
  Button button_9 (.out(b13));
  Button button_10 (.out(b2));
  Button button_11 (.out(b3));
  Button button_12 (.out(b6));
  Button button_13 (.out(b7));
  Button button_14 (.out(b11));
  Button button_15 (.out(b10));
  Button button_16 (.out(b14));
  Button button_17 (.out(b15));
  or or_2 (sigAnyPress, b0, b1, b2, b3, b4, b5, b6, b7, b8, b9, b10, b11, b12, b13, b14, b15);
  nor nor_1 (sigWin, l0, l1, l2, l3, l4, l5, l6, l7, l8, l9, l10, l11, l12, l13, l14, l15);
  Random #(.width(16)) random_1 (.next(1'b1), .clk(sigReset), .out(sigPreset));  // open: clr
  or or_3 (sigAddr[0], b1, b3, b5, b7, b9, b11, b13, b15);
  or or_4 (sigAddr[1], b2, b3, b6, b7, b10, b11, b14, b15);
  or or_5 (sigAddr[2], b4, b5, b6, b7, b12, b13, b14, b15);
  or or_6 (sigAddr[3], b8, b9, b10, b11, b12, b13, b14, b15);
  ROM #(.addrWidth(4), .dataWidth(16)) rom_1 (.addr(sigAddr), .data(sigMask));
  Counter counter_1 (.clr(sigReset), .clk(sigAnyPress), .Q(sigMoves));  // open: load, up, count, D, carry

  // Other names for the same wires on the sheet: sigState[15:0] = {l15, l14, l13, l12, l11, l10, l9, l8, l7, l6, l5, l4, l3, l2, l1, l0}

  // Notes on the sheet:
  //   GAME CONTROLS
  //   RESET GAME
  //   MOVE COUNTER
  //   VICTORY STATUS
  //   State Tracker
  //   Select Poke Tool (Finger) -> Click any Button in the 4x4 Grid to toggle it & its neighbors.
  //   State Register
  //   Lights
  //   LIGHTS OUT (4x4 Version)
  //   Turn ALL 16 lights OFF to WIN!
  //   Buttons
  //   Any Button Press Detector
  //   Win Detector (1 if All lights are off)
  //   Button Encoder (16 to 4 bit)
  //   Random State Generator
  //   contents of rom_1 (hex, n*v repeats v):
  //   13 27 4e 8c 131 272 4e4 8c8 1310 2720 4e40 8c80 3100 7200 e400 c800
  //   BITMASK ROM (Consists of preset of each button)
  //    Move Counter
endmodule
